# Fritzing sketch pico_prototype (saved by Fritzing 1.0.1rc)
circuit board: 12.3802cm x 9.08754cm
breadboards: 1

parts:
  Pico_W = Raspberry Pi Pico W
  Speed_Control = Rotary Potentiometer (Large) [maximum_resistance=100kΩ knob_status=50% package=THT]
  Forward = Momentary Switch [package=tactile-pth]
  Right = Momentary Switch [package=tactile-pth]
  Left = Momentary Switch [package=tactile-pth]
  Backward = Momentary Switch [package=tactile-pth]
  LED1 = LED - 5mm [color="Red (633nm)" current=0.030 package="5 mm [THT]"]
  R1 = Resistor [tolerance=±5% power=0.25 resistance=330 package=THT]

nets:
  N1: Pico_W.pin_1, Backward.1
  N2: Pico_W.pin_4, Forward.1
  N3: Pico_W.pin_5, LED1.anode
  N4: Pico_W.pin_13, Pico_W.pin_18, Pico_W.pin_23, Pico_W.pin_33, Speed_Control.leg2, Forward.4, Right.3, Left.1, Backward.4, R1.Pin_1
  N5: Pico_W.pin_19, Right.2
  N6: Pico_W.pin_20, Left.4
  N7: Pico_W.pin_31, Speed_Control.wiper
  N8: Pico_W.pin_36, Speed_Control.leg1
  N9: LED1.cathode, R1.Pin_0

notes:
  Pico W Controller Phase 2

custom parts:
  Raspberry Pi Pico W: Raspberry Pi Pico W. Based around the RP2040 microcontroller the Pico W is a low cost microcontroller device bringing Raspberry Pi quality, cost, and easy of use to the microcontroller space. The areas marked KEEPOUT in pcb silkscreen should not have traces running through them to avoid shorts on a soldered in module!
